# Fritzing sketch Matrix-project (saved by Fritzing 0.8.7b)
breadboards: 3

parts:
  Part1 = SRF05  # not connected
  Disp1 = KWM-R30881CUAB [part_number=KWM-R30881CUAB]
  U1 = MAX7219 [package=dil24]
  U2 = LCD-16X2 [package=lcd-16x2]
  Part3 = KY-023 Dual Axis Joystick Module [package="Breakout board"]
  Part4 = Arduino Uno (Rev3)
  R1 = Resistor [tolerance=±5% resistance=10k package=THT]
  J1 = Piezo Speaker
  R2 = Resistor [tolerance=±5% resistance=100 package=THT]
  C1 = Capacitor [package=cap-pth-small2]
  C2 = Electrolytic Capacitor [capacitance=10µF package="100 mil [THT, electrolytic]"]
  U3 = POT [package=pot_alpha_rv16af-20]
  R3 = Resistor [tolerance=±5% resistance=220 package=THT]

nets:
  N1: Disp1.pin1, U1.DIG4
  N2: Disp1.pin2, U1.DIG6
  N3: Disp1.pin_3, U1.SEGA
  N4: Disp1.pin_4, U1.SEGB
  N5: Disp1.pin_5, U1.DIG7
  N6: Disp1.pin_6, U1.SEGD
  N7: Disp1.pin_7, U1.DIG5
  N8: Disp1.pin_8, U1.DIG2
  N9: Disp1.pin_9, U1.DIG0
  N10: Disp1.pin_10, U1.SEGC
  N11: Disp1.pin_11, U1.SEGE
  N12: Disp1.pin_12, U1.DIG3
  N13: Disp1.pin_13, U1.SEGDP
  N14: Disp1.pin_14, U1.DIG1
  N15: Disp1.pin_15, U1.SEGF
  N16: Disp1.pin_16, U1.SEGG
  N17: U1.DIN, Part4.D12/MISO
  GND: U1.GND, U1.GND2, U2.VSS, U2.R_W, U2.K, Part3.GND, R1.Pin_0, J1.pin1, C1.2, C2.-
  N18: U1.LOAD, Part4.D10_PWM/SS
  N19: U1.CLK, Part4.D11_PWM/MOSI
  N20: U1.ISET, R1.Pin_1
  VCC: U1.VCC, U2.VDD, Part3.+5V, C1.1, C2.+, U3.E, R3.Pin_1
  N21: U2.VO, U3.S
  N22: U2.RS, Part4.D7
  N23: U2.E, Part4.D6_PWM
  N24: U2.DB4, Part4.D5_PWM
  N25: U2.DB5, Part4.D4
  N26: U2.DB6, Part4.D3_PWM
  N27: U2.DB7, Part4.D2
  N28: U2.A, R3.Pin_0
  N29: Part3.VRx, Part4.A0
  N30: Part3.VRy, Part4.A1
  N31: Part3.SW, Part4.D8
  N32: Part4.D13/SCK, R2.Pin_0
  N33: J1.pin2, R2.Pin_1

custom parts:
  KWM-R30881CUAB: LED Matrix Display 8x8 red 60.5mm modified for KWM-R30881CUAB row cathode feb 2018.
